// Logisim project game_final_version.circ as structural Verilog: 18 circuits, main circuit main
module main (
);

  wire collisioncombo_1_out_27, comparator_1_eq, D_out, digitalscore_1_out_2, digitalscore_1_out_3,
       digitalscore_1_out_4, digitalscore_1_out_5, digitalscore_1_out_6, digitalscore_1_out_7,
       digitalscore_1_out_8, disablers_1_downout, disablers_1_leftout, disablers_1_rightout,
       disablers_1_upout, L_out, multiplexer_1_out, multiplexer_2_out, not_1_out, or_1_out, or_2_out,
       or_3_out, R_out, speedup_1_clockout, Start_Reset_out, U_out, up_down_1_countertrigger;
  wire [3:0] counter_1_q, left_right_1_out, up_down_1_out;
  wire [6:0] checkgame_1_out_3, checkgame_1_out_4, checkgame_1_out_5, checkgame_1_out_6, checkgame_1_out_7,
       checkgame_1_out_8, checkgame_1_out_9, checkgame_1_out_10, checkgame_1_out_11, checkgame_1_out_12,
       checkgame_1_out_13, checkgame_1_out_14, checkgame_1_out_15, checkgame_1_out_16, checkgame_1_out_17,
       checkgame_1_out_18, checkgame_1_out_19, checkgame_1_out_20, checkgame_1_out_21, checkgame_1_out_22,
       checkgame_1_out_23, checkgame_1_out_24, checkgame_1_out_25, checkgame_1_out_26, checkgame_1_out_27,
       checkgame_1_out_28, checkgame_1_out_29, checkgame_1_out_30, checkgame_1_out_31, checkgame_1_out_32,
       checkgame_1_out_33, checkgame_1_out_34;
  wire [12:0] columncombo_1_out_27, columncombo_1_out_28, columncombo_1_out_29, columncombo_1_out_30,
       columncombo_1_out_31, columncombo_1_out_32, columncombo_1_out_33, columncombo_1_out_34,
       columncombo_1_out_35, columncombo_1_out_36, columncombo_1_out_37, columncombo_1_out_38,
       columncombo_1_out_39, columnshifter_1_out_3, columnshifter_1_out_4, columnshifter_1_out_5,
       columnshifter_1_out_6, columnshifter_1_out_7, columnshifter_1_out_8, columnshifter_1_out_9,
       columnshifter_1_out_10, columnshifter_1_out_11, columnshifter_1_out_12, columnshifter_1_out_13,
       columnshifter_1_out_14, columnshifter_1_out_15, demultiplexer_1_out0, demultiplexer_1_out1,
       demultiplexer_1_out2, demultiplexer_1_out3, demultiplexer_1_out4, demultiplexer_1_out5,
       demultiplexer_1_out6, demultiplexer_1_out7, demultiplexer_1_out8, demultiplexer_1_out9,
       demultiplexer_1_out10, demultiplexer_1_out11, demultiplexer_1_out12, rom_1_data;

  speedUp speedup_1 (.clockChoose(counter_1_q), .clockOut(speedup_1_clockout));
  Multiplexer #(.enable("false")) multiplexer_1 (
    .in0(speedup_1_clockout), .out(multiplexer_1_out), .sel(or_1_out));  // open: in1
  or or_1 (or_1_out, comparator_1_eq, collisioncombo_1_out_27);
  or or_2 (or_2_out, comparator_1_eq, collisioncombo_1_out_27);
  left_right left_right_1 (
    .out(left_right_1_out), .reset(Start_Reset_out), .left(disablers_1_leftout), .right(disablers_1_rightout));
  columnShifter columnshifter_1 (
    .Clock_in(multiplexer_1_out), .Reset(Start_Reset_out), .out_3(columnshifter_1_out_3),
    .out_4(columnshifter_1_out_4), .out_5(columnshifter_1_out_5), .out_6(columnshifter_1_out_6),
    .out_7(columnshifter_1_out_7), .out_8(columnshifter_1_out_8), .out_9(columnshifter_1_out_9),
    .out_10(columnshifter_1_out_10), .out_11(columnshifter_1_out_11), .out_12(columnshifter_1_out_12),
    .out_13(columnshifter_1_out_13), .out_14(columnshifter_1_out_14), .out_15(columnshifter_1_out_15));
  collisionCombo collisioncombo_1 (
    .in_1(columnshifter_1_out_3), .in_2(demultiplexer_1_out0), .in_3(columnshifter_1_out_4),
    .in_4(demultiplexer_1_out1), .in_5(columnshifter_1_out_5), .in_6(demultiplexer_1_out2),
    .in_7(columnshifter_1_out_6), .in_8(demultiplexer_1_out3), .in_9(columnshifter_1_out_7),
    .in_10(demultiplexer_1_out4), .in_11(columnshifter_1_out_8), .in_12(demultiplexer_1_out5),
    .in_13(columnshifter_1_out_9), .in_14(demultiplexer_1_out6), .in_15(columnshifter_1_out_10),
    .in_16(demultiplexer_1_out7), .in_17(columnshifter_1_out_11), .in_18(demultiplexer_1_out8),
    .in_19(columnshifter_1_out_12), .in_20(demultiplexer_1_out9), .in_21(columnshifter_1_out_13),
    .in_22(demultiplexer_1_out10), .in_23(columnshifter_1_out_14), .in_24(demultiplexer_1_out11),
    .in_25(columnshifter_1_out_15), .in_26(demultiplexer_1_out12), .out_27(collisioncombo_1_out_27));
  up_down up_down_1 (
    .counterTrigger(up_down_1_countertrigger), .out(up_down_1_out), .down(disablers_1_downout),
    .up(disablers_1_upout), .reset(Start_Reset_out));
  ROM #(.addrWidth(4), .dataWidth(13)) rom_1 (.addr(up_down_1_out), .data(rom_1_data));  // open: sel
  columnCombo columncombo_1 (
    .in_14(demultiplexer_1_out0), .in_1(columnshifter_1_out_3), .in_15(demultiplexer_1_out1),
    .in_2(columnshifter_1_out_4), .in_16(demultiplexer_1_out2), .in_3(columnshifter_1_out_5),
    .in_17(demultiplexer_1_out3), .in_4(columnshifter_1_out_6), .in_18(demultiplexer_1_out4),
    .in_5(columnshifter_1_out_7), .in_19(demultiplexer_1_out5), .in_6(columnshifter_1_out_8),
    .in_20(demultiplexer_1_out6), .in_7(columnshifter_1_out_9), .in_21(demultiplexer_1_out7),
    .in_8(columnshifter_1_out_10), .in_22(demultiplexer_1_out8), .in_9(columnshifter_1_out_11),
    .in_23(demultiplexer_1_out9), .in_10(columnshifter_1_out_12), .in_24(demultiplexer_1_out10),
    .in_11(columnshifter_1_out_13), .in_25(demultiplexer_1_out11), .in_12(columnshifter_1_out_14),
    .in_26(demultiplexer_1_out12), .in_13(columnshifter_1_out_15), .out_27(columncombo_1_out_27),
    .out_28(columncombo_1_out_28), .out_29(columncombo_1_out_29), .out_30(columncombo_1_out_30),
    .out_31(columncombo_1_out_31), .out_32(columncombo_1_out_32), .out_33(columncombo_1_out_33),
    .out_34(columncombo_1_out_34), .out_35(columncombo_1_out_35), .out_36(columncombo_1_out_36),
    .out_37(columncombo_1_out_37), .out_38(columncombo_1_out_38), .out_39(columncombo_1_out_39));
  Demultiplexer #(.select(4), .width(13), .enable("false")) demultiplexer_1 (
    .out0(demultiplexer_1_out0), .out1(demultiplexer_1_out1), .out2(demultiplexer_1_out2),
    .out3(demultiplexer_1_out3), .out4(demultiplexer_1_out4), .out5(demultiplexer_1_out5),
    .out6(demultiplexer_1_out6), .out7(demultiplexer_1_out7), .out8(demultiplexer_1_out8),
    .out9(demultiplexer_1_out9), .out10(demultiplexer_1_out10), .out11(demultiplexer_1_out11),
    .out12(demultiplexer_1_out12), .in(rom_1_data), .sel(left_right_1_out));  // open: out13, out14, out15
  disablers disablers_1 (
    .upIn(U_out), .downIn(D_out), .rightIn(R_out), .leftIn(L_out), .upOut(disablers_1_upout),
    .downOut(disablers_1_downout), .rightOut(disablers_1_rightout), .leftOut(disablers_1_leftout),
    .enable(or_2_out));
  DotMatrix #(.matrixcols(32)) dotmatrix_1 (
    .col0(checkgame_1_out_3), .col1(checkgame_1_out_4), .col2(checkgame_1_out_5), .col3(checkgame_1_out_6),
    .col4(checkgame_1_out_7), .col5(checkgame_1_out_8), .col6(checkgame_1_out_9), .col7(checkgame_1_out_10),
    .col8(checkgame_1_out_11), .col9(checkgame_1_out_12), .col10(checkgame_1_out_13),
    .col11(checkgame_1_out_14), .col12(checkgame_1_out_15), .col13(checkgame_1_out_16),
    .col14(checkgame_1_out_17), .col15(checkgame_1_out_18), .col16(checkgame_1_out_19),
    .col17(checkgame_1_out_20), .col18(checkgame_1_out_21), .col19(checkgame_1_out_22),
    .col20(checkgame_1_out_23), .col21(checkgame_1_out_24), .col22(checkgame_1_out_25),
    .col23(checkgame_1_out_26), .col24(checkgame_1_out_27), .col25(checkgame_1_out_28),
    .col26(checkgame_1_out_29), .col27(checkgame_1_out_30), .col28(checkgame_1_out_31),
    .col29(checkgame_1_out_32), .col30(checkgame_1_out_33), .col31(checkgame_1_out_34));
  DotMatrix #(.matrixcols(13), .matrixrows(13)) dotmatrix_2 (
    .col0(columncombo_1_out_27), .col1(columncombo_1_out_28), .col2(columncombo_1_out_29),
    .col3(columncombo_1_out_30), .col4(columncombo_1_out_31), .col5(columncombo_1_out_32),
    .col6(columncombo_1_out_33), .col7(columncombo_1_out_34), .col8(columncombo_1_out_35),
    .col9(columncombo_1_out_36), .col10(columncombo_1_out_37), .col11(columncombo_1_out_38),
    .col12(columncombo_1_out_39));
  Button L (.out(L_out));
  Button U (.out(U_out));
  Button R (.out(R_out));
  Button D (.out(D_out));
  Counter #(.width(4), .max('h5)) counter_1 (
    .Q(counter_1_q), .clk(up_down_1_countertrigger), .clr(Start_Reset_out));  // open: load, D, count, carry
  Button Start_Reset (.out(Start_Reset_out));
  checkGame checkgame_1 (
    .out_3(checkgame_1_out_3), .out_4(checkgame_1_out_4), .out_5(checkgame_1_out_5),
    .out_6(checkgame_1_out_6), .out_7(checkgame_1_out_7), .out_8(checkgame_1_out_8),
    .out_9(checkgame_1_out_9), .out_10(checkgame_1_out_10), .out_11(checkgame_1_out_11),
    .out_12(checkgame_1_out_12), .out_13(checkgame_1_out_13), .out_14(checkgame_1_out_14),
    .out_15(checkgame_1_out_15), .out_16(checkgame_1_out_16), .out_17(checkgame_1_out_17),
    .out_18(checkgame_1_out_18), .out_19(checkgame_1_out_19), .out_20(checkgame_1_out_20),
    .out_21(checkgame_1_out_21), .out_22(checkgame_1_out_22), .out_23(checkgame_1_out_23),
    .out_24(checkgame_1_out_24), .out_25(checkgame_1_out_25), .out_26(checkgame_1_out_26),
    .out_27(checkgame_1_out_27), .out_28(checkgame_1_out_28), .out_29(checkgame_1_out_29),
    .out_30(checkgame_1_out_30), .out_31(checkgame_1_out_31), .out_32(checkgame_1_out_32),
    .out_33(checkgame_1_out_33), .out_34(checkgame_1_out_34), .in_1(multiplexer_2_out), .in_2(or_3_out));
  digitalScore digitalscore_1 (
    .in_1(counter_1_q), .out_2(digitalscore_1_out_2), .out_3(digitalscore_1_out_3),
    .out_4(digitalscore_1_out_4), .out_5(digitalscore_1_out_5), .out_6(digitalscore_1_out_6),
    .out_7(digitalscore_1_out_7), .out_8(digitalscore_1_out_8));
  _7_Segment_Display u_7_segment_display_1 (
    .g(digitalscore_1_out_8), .f(digitalscore_1_out_7), .a(digitalscore_1_out_2), .b(digitalscore_1_out_3),
    .e(digitalscore_1_out_6), .d(digitalscore_1_out_5), .c(digitalscore_1_out_4));  // open: dp
  Comparator #(.width(4)) comparator_1 (.a(counter_1_q), .b(4'b0101), .eq(comparator_1_eq));  // open: gt, lt
  not not_1 (not_1_out, or_1_out);
  or or_3 (or_3_out, comparator_1_eq, or_1_out);
  Multiplexer #(.enable("false")) multiplexer_2 (
    .in0(not_1_out), .in1(comparator_1_eq), .out(multiplexer_2_out), .sel(comparator_1_eq));

  // Notes on the sheet:
  //   contents of rom_1 (hex, n*v repeats v):
  //   1 2 4 8 10 20 40 80 100 200 400 800 1000
  //   Recommended Clock Setting: 16Hz
endmodule

module adder (
  input  [3:0] Cin,
  output [3:0] Out
);

  Adder #(.width(4)) adder_1 (.a(Cin), .b(4'b0001), .out(Out));  // open: cin, cout
endmodule

module subtractor (
  input  [3:0] Cin,
  output [3:0] Out
);

  Subtractor #(.width(4)) subtractor_1 (.a(Cin), .b(4'b0001), .out(Out));  // open: bin, bout
endmodule

module up_down (
  input  down,
  input  up,
  input  reset,
  output [3:0] out,
  output counterTrigger
);

  wire comparator_1_eq, or_1_out, or_2_out;
  wire [3:0] adder_1_out, multiplexer_1_out, subtractor_1_out;

  adder adder_1 (.Cin(out), .Out(adder_1_out));
  subtractor subtractor_1 (.Cin(out), .Out(subtractor_1_out));
  Multiplexer #(.width(4), .enable("false")) multiplexer_1 (
    .in0(adder_1_out), .in1(subtractor_1_out), .out(multiplexer_1_out), .sel(down));
  Register #(.width(4), .trigger("falling")) register_1 (
    .D(multiplexer_1_out), .Q(out), .clk(or_1_out), .clr(or_2_out));  // open: en
  or or_1 (or_1_out, up, down);
  or or_2 (or_2_out, counterTrigger, comparator_1_eq, reset);
  Comparator #(.width(4)) comparator_1 (.a(multiplexer_1_out), .b(4'b1111), .eq(comparator_1_eq));  // open: gt, lt
  Comparator #(.width(4)) comparator_2 (.a(out), .b(4'b1101), .eq(counterTrigger));  // open: gt, lt
endmodule

module left_right (
  input  reset,
  input  left,
  input  right,
  output [3:0] out
);

  wire comparator_1_eq, comparator_2_eq, or_1_out;
  wire [3:0] adder_1_out, multiplexer_1_out, multiplexer_2_out, register_1_q, subtractor_1_out;

  adder adder_1 (.Cin(out), .Out(adder_1_out));
  subtractor subtractor_1 (.Cin(out), .Out(subtractor_1_out));
  Multiplexer #(.width(4), .enable("false")) multiplexer_1 (
    .in0(adder_1_out), .in1(subtractor_1_out), .out(multiplexer_1_out), .sel(left));
  Multiplexer #(.width(4), .enable("false")) multiplexer_2 (
    .in0(multiplexer_1_out), .in1(4'b0110), .out(multiplexer_2_out), .sel(reset));
  Register #(.width(4), .trigger("falling")) register_1 (
    .D(multiplexer_2_out), .Q(register_1_q), .clk(or_1_out), .clr(comparator_1_eq));  // open: en
  or or_1 (or_1_out, right, left, reset);
  Multiplexer #(.width(4), .enable("false")) multiplexer_3 (
    .in0(register_1_q), .in1(4'b1100), .out(out), .sel(comparator_2_eq));
  Comparator #(.width(4)) comparator_1 (.a(multiplexer_2_out), .b(4'b1111), .eq(comparator_1_eq));  // open: gt, lt
  Comparator #(.width(4)) comparator_2 (.a(register_1_q), .b(4'b1101), .eq(comparator_2_eq));  // open: gt, lt
endmodule

module columnShifter (
  input  Clock_in,
  input  Reset,
  output [12:0] out_3,
  output [12:0] out_4,
  output [12:0] out_5,
  output [12:0] out_6,
  output [12:0] out_7,
  output [12:0] out_8,
  output [12:0] out_9,
  output [12:0] out_10,
  output [12:0] out_11,
  output [12:0] out_12,
  output [12:0] out_13,
  output [12:0] out_14,
  output [12:0] out_15
);

  wire [12:0] randomsheep_1_out_1;

  randomSheep randomsheep_1 (.out_1(randomsheep_1_out_1));
  Register #(.width(13)) register_1 (.D(randomsheep_1_out_1), .Q(out_3), .clk(Clock_in), .clr(Reset));  // open: en
  Register #(.width(13)) register_2 (.D(out_3), .Q(out_4), .clk(Clock_in), .clr(Reset));  // open: en
  Register #(.width(13)) register_3 (.D(out_4), .Q(out_5), .clk(Clock_in), .clr(Reset));  // open: en
  Register #(.width(13)) register_4 (.D(out_5), .Q(out_6), .clk(Clock_in), .clr(Reset));  // open: en
  Register #(.width(13)) register_5 (.D(out_6), .Q(out_7), .clk(Clock_in), .clr(Reset));  // open: en
  Register #(.width(13)) register_6 (.D(out_7), .Q(out_8), .clk(Clock_in), .clr(Reset));  // open: en
  Register #(.width(13)) register_7 (.D(out_8), .Q(out_9), .clk(Clock_in), .clr(Reset));  // open: en
  Register #(.width(13)) register_8 (.D(out_9), .Q(out_10), .clk(Clock_in), .clr(Reset));  // open: en
  Register #(.width(13)) register_9 (.D(out_10), .Q(out_11), .clk(Clock_in), .clr(Reset));  // open: en
  Register #(.width(13)) register_10 (.D(out_11), .Q(out_12), .clk(Clock_in), .clr(Reset));  // open: en
  Register #(.width(13)) register_11 (.D(out_12), .Q(out_13), .clk(Clock_in), .clr(Reset));  // open: en
  Register #(.width(13)) register_12 (.D(out_13), .Q(out_14), .clk(Clock_in), .clr(Reset));  // open: en
  Register #(.width(13)) register_13 (.D(out_14), .Q(out_15), .clk(Clock_in), .clr(Reset));  // open: en
endmodule

module randomSheep (
  output [12:0] out_1
);

  wire clock_1_out;
  wire [12:0] random_1_out;

  Clock clock_1 (.out(clock_1_out));
  Random #(.width(13)) random_1 (.clk(clock_1_out), .out(random_1_out));  // open: next, clr
  assign out_1 = random_1_out & 13'h1252;  // AND_Gate and_1, 13 bits wide

  // Notes on the sheet:
  //   Random 13 bit string
  //   1 0010 0101 0010
  //   Creates gaps
endmodule

module columnCombo (
  input  [12:0] in_1,
  input  [12:0] in_2,
  input  [12:0] in_3,
  input  [12:0] in_4,
  input  [12:0] in_5,
  input  [12:0] in_6,
  input  [12:0] in_7,
  input  [12:0] in_8,
  input  [12:0] in_9,
  input  [12:0] in_10,
  input  [12:0] in_11,
  input  [12:0] in_12,
  input  [12:0] in_13,
  input  [12:0] in_14,
  input  [12:0] in_15,
  input  [12:0] in_16,
  input  [12:0] in_17,
  input  [12:0] in_18,
  input  [12:0] in_19,
  input  [12:0] in_20,
  input  [12:0] in_21,
  input  [12:0] in_22,
  input  [12:0] in_23,
  input  [12:0] in_24,
  input  [12:0] in_25,
  input  [12:0] in_26,
  output [12:0] out_27,
  output [12:0] out_28,
  output [12:0] out_29,
  output [12:0] out_30,
  output [12:0] out_31,
  output [12:0] out_32,
  output [12:0] out_33,
  output [12:0] out_34,
  output [12:0] out_35,
  output [12:0] out_36,
  output [12:0] out_37,
  output [12:0] out_38,
  output [12:0] out_39
);

  assign out_27 = in_14 ^ in_1;  // XOR_Gate xor_1, 13 bits wide
  assign out_28 = in_15 ^ in_2;  // XOR_Gate xor_2, 13 bits wide
  assign out_29 = in_16 ^ in_3;  // XOR_Gate xor_3, 13 bits wide
  assign out_30 = in_17 ^ in_4;  // XOR_Gate xor_4, 13 bits wide
  assign out_31 = in_18 ^ in_5;  // XOR_Gate xor_5, 13 bits wide
  assign out_32 = in_19 ^ in_6;  // XOR_Gate xor_6, 13 bits wide
  assign out_33 = in_20 ^ in_7;  // XOR_Gate xor_7, 13 bits wide
  assign out_34 = in_21 ^ in_8;  // XOR_Gate xor_8, 13 bits wide
  assign out_35 = in_22 ^ in_9;  // XOR_Gate xor_9, 13 bits wide
  assign out_36 = in_23 ^ in_10;  // XOR_Gate xor_10, 13 bits wide
  assign out_37 = in_24 ^ in_11;  // XOR_Gate xor_11, 13 bits wide
  assign out_38 = in_25 ^ in_12;  // XOR_Gate xor_12, 13 bits wide
  assign out_39 = in_26 ^ in_13;  // XOR_Gate xor_13, 13 bits wide
endmodule

module collisionDetection (
  input  [12:0] in_1,
  input  [12:0] in_2,
  output out_3
);

  wire [12:0] and_1_out;

  assign and_1_out = in_1 & in_2;  // AND_Gate and_1, 13 bits wide
  or or_1 (out_3, and_1_out[0], and_1_out[1], and_1_out[2], and_1_out[3], and_1_out[4], and_1_out[5], and_1_out[6], and_1_out[7], and_1_out[8], and_1_out[9], and_1_out[10], and_1_out[11], and_1_out[12]);
endmodule

module collisionCombo (
  input  [12:0] in_1,
  input  [12:0] in_2,
  input  [12:0] in_3,
  input  [12:0] in_4,
  input  [12:0] in_5,
  input  [12:0] in_6,
  input  [12:0] in_7,
  input  [12:0] in_8,
  input  [12:0] in_9,
  input  [12:0] in_10,
  input  [12:0] in_11,
  input  [12:0] in_12,
  input  [12:0] in_13,
  input  [12:0] in_14,
  input  [12:0] in_15,
  input  [12:0] in_16,
  input  [12:0] in_17,
  input  [12:0] in_18,
  input  [12:0] in_19,
  input  [12:0] in_20,
  input  [12:0] in_21,
  input  [12:0] in_22,
  input  [12:0] in_23,
  input  [12:0] in_24,
  input  [12:0] in_25,
  input  [12:0] in_26,
  output out_27
);

  wire collisiondetection_1_out_3, collisiondetection_2_out_3, collisiondetection_3_out_3,
       collisiondetection_4_out_3, collisiondetection_5_out_3, collisiondetection_6_out_3,
       collisiondetection_7_out_3, collisiondetection_8_out_3, collisiondetection_9_out_3,
       collisiondetection_10_out_3, collisiondetection_11_out_3, collisiondetection_12_out_3,
       collisiondetection_13_out_3;

  collisionDetection collisiondetection_1 (.out_3(collisiondetection_1_out_3), .in_1(in_1), .in_2(in_2));
  collisionDetection collisiondetection_2 (.out_3(collisiondetection_2_out_3), .in_1(in_3), .in_2(in_4));
  collisionDetection collisiondetection_3 (.out_3(collisiondetection_3_out_3), .in_1(in_5), .in_2(in_6));
  collisionDetection collisiondetection_4 (.out_3(collisiondetection_4_out_3), .in_1(in_7), .in_2(in_8));
  collisionDetection collisiondetection_5 (.out_3(collisiondetection_5_out_3), .in_1(in_9), .in_2(in_10));
  collisionDetection collisiondetection_6 (.out_3(collisiondetection_6_out_3), .in_1(in_11), .in_2(in_12));
  collisionDetection collisiondetection_7 (.out_3(collisiondetection_7_out_3), .in_1(in_13), .in_2(in_14));
  collisionDetection collisiondetection_8 (.out_3(collisiondetection_8_out_3), .in_1(in_15), .in_2(in_16));
  collisionDetection collisiondetection_9 (.out_3(collisiondetection_9_out_3), .in_1(in_17), .in_2(in_18));
  collisionDetection collisiondetection_10 (.out_3(collisiondetection_10_out_3), .in_1(in_19), .in_2(in_20));
  collisionDetection collisiondetection_11 (.out_3(collisiondetection_11_out_3), .in_1(in_21), .in_2(in_22));
  collisionDetection collisiondetection_12 (.out_3(collisiondetection_12_out_3), .in_1(in_23), .in_2(in_24));
  collisionDetection collisiondetection_13 (.out_3(collisiondetection_13_out_3), .in_1(in_25), .in_2(in_26));
  or or_1 (out_27, collisiondetection_1_out_3, collisiondetection_2_out_3, collisiondetection_3_out_3, collisiondetection_4_out_3, collisiondetection_5_out_3, collisiondetection_6_out_3, collisiondetection_7_out_3, collisiondetection_8_out_3, collisiondetection_9_out_3, collisiondetection_10_out_3, collisiondetection_11_out_3, collisiondetection_12_out_3, collisiondetection_13_out_3);
endmodule

module digitalScore (
  input  [3:0] in_1,
  output out_2,
  output out_3,
  output out_4,
  output out_5,
  output out_6,
  output out_7,
  output out_8
);

  wire comparator_1_eq, comparator_2_eq, comparator_3_eq, comparator_4_eq, comparator_5_eq, comparator_6_eq,
       comparator_7_eq, comparator_8_eq, comparator_9_eq, comparator_10_eq;

  Comparator #(.width(4)) comparator_1 (.a(in_1), .b(4'b0000), .eq(comparator_1_eq));  // open: gt, lt
  Comparator #(.width(4)) comparator_2 (.a(in_1), .b(4'b0001), .eq(comparator_2_eq));  // open: gt, lt
  Comparator #(.width(4)) comparator_3 (.a(in_1), .b(4'b0010), .eq(comparator_3_eq));  // open: gt, lt
  Comparator #(.width(4)) comparator_4 (.a(in_1), .b(4'b0011), .eq(comparator_4_eq));  // open: gt, lt
  Comparator #(.width(4)) comparator_5 (.a(in_1), .b(4'b0100), .eq(comparator_5_eq));  // open: gt, lt
  Comparator #(.width(4)) comparator_6 (.a(in_1), .b(4'b0101), .eq(comparator_6_eq));  // open: gt, lt
  Comparator #(.width(4)) comparator_7 (.a(in_1), .b(4'b0110), .eq(comparator_7_eq));  // open: gt, lt
  Comparator #(.width(4)) comparator_8 (.a(in_1), .b(4'b0111), .eq(comparator_8_eq));  // open: gt, lt
  Comparator #(.width(4)) comparator_9 (.a(in_1), .b(4'b1000), .eq(comparator_9_eq));  // open: gt, lt
  Comparator #(.width(4)) comparator_10 (.a(in_1), .b(4'b1001), .eq(comparator_10_eq));  // open: gt, lt
  or a (out_2, comparator_1_eq, comparator_3_eq, comparator_4_eq, comparator_6_eq, comparator_7_eq, comparator_8_eq, comparator_9_eq, comparator_10_eq);
  or b (out_3, comparator_1_eq, comparator_2_eq, comparator_3_eq, comparator_4_eq, comparator_5_eq, comparator_8_eq, comparator_9_eq, comparator_10_eq);
  or c (out_4, comparator_1_eq, comparator_2_eq, comparator_4_eq, comparator_5_eq, comparator_6_eq, comparator_7_eq, comparator_8_eq, comparator_9_eq, comparator_10_eq);
  or d (out_5, comparator_1_eq, comparator_3_eq, comparator_4_eq, comparator_6_eq, comparator_7_eq, comparator_9_eq, comparator_10_eq);
  or e (out_6, comparator_1_eq, comparator_3_eq, comparator_7_eq, comparator_9_eq);
  or f (out_7, comparator_1_eq, comparator_5_eq, comparator_6_eq, comparator_7_eq, comparator_9_eq, comparator_10_eq);
  or g (out_8, comparator_3_eq, comparator_4_eq, comparator_5_eq, comparator_6_eq, comparator_7_eq, comparator_9_eq, comparator_10_eq);
endmodule

module win (
  output [6:0] out_1,
  output [6:0] out_2,
  output [6:0] out_3,
  output [6:0] out_4,
  output [6:0] out_5,
  output [6:0] out_6,
  output [6:0] out_7,
  output [6:0] out_8,
  output [6:0] out_9,
  output [6:0] out_10,
  output [6:0] out_11,
  output [6:0] out_12,
  output [6:0] out_13,
  output [6:0] out_14,
  output [6:0] out_15,
  output [6:0] out_16,
  output [6:0] out_17,
  output [6:0] out_18,
  output [6:0] out_19,
  output [6:0] out_20,
  output [6:0] out_21,
  output [6:0] out_22,
  output [6:0] out_23,
  output [6:0] out_24,
  output [6:0] out_25,
  output [6:0] out_26,
  output [6:0] out_27,
  output [6:0] out_28,
  output [6:0] out_29,
  output [6:0] out_30,
  output [6:0] out_31,
  output [6:0] out_32
);


  assign out_1 = {7{1'b0}};
  assign out_2 = 7'b0111000;
  assign out_3 = 7'b0001110;
  assign out_4 = 7'b0111000;
  assign out_5 = {7{1'b0}};
  assign out_6 = 7'b0111110;
  assign out_7 = 7'b0100010;
  assign out_8 = 7'b0111110;
  assign out_9 = {7{1'b0}};
  assign out_10 = 7'b0111110;
  assign out_11 = 7'b0000010;
  assign out_12 = 7'b0111110;
  assign out_13 = {7{1'b0}};
  assign out_14 = {7{1'b0}};
  assign out_15 = 7'b0111110;
  assign out_16 = 7'b0000100;
  assign out_17 = 7'b0011000;
  assign out_18 = 7'b0000100;
  assign out_19 = 7'b0111110;
  assign out_20 = {7{1'b0}};
  assign out_21 = 7'b0100010;
  assign out_22 = 7'b0111110;
  assign out_23 = 7'b0100010;
  assign out_24 = {7{1'b0}};
  assign out_25 = 7'b0111110;
  assign out_26 = 7'b0010000;
  assign out_27 = 7'b0001000;
  assign out_28 = 7'b0000100;
  assign out_29 = 7'b0111110;
  assign out_30 = {7{1'b0}};
  assign out_31 = {7{1'b0}};
  assign out_32 = {7{1'b0}};
endmodule

module lose (
  output [6:0] out_1,
  output [6:0] out_2,
  output [6:0] out_3,
  output [6:0] out_4,
  output [6:0] out_5,
  output [6:0] out_6,
  output [6:0] out_7,
  output [6:0] out_8,
  output [6:0] out_9,
  output [6:0] out_10,
  output [6:0] out_11,
  output [6:0] out_12,
  output [6:0] out_13,
  output [6:0] out_14,
  output [6:0] out_15,
  output [6:0] out_16,
  output [6:0] out_17,
  output [6:0] out_18,
  output [6:0] out_19,
  output [6:0] out_20,
  output [6:0] out_21,
  output [6:0] out_22,
  output [6:0] out_23,
  output [6:0] out_24,
  output [6:0] out_25,
  output [6:0] out_26,
  output [6:0] out_27,
  output [6:0] out_28,
  output [6:0] out_29,
  output [6:0] out_30,
  output [6:0] out_31,
  output [6:0] out_32
);


  assign out_1 = {7{1'b0}};
  assign out_2 = 7'b0111000;
  assign out_3 = 7'b0001110;
  assign out_4 = 7'b0111000;
  assign out_5 = {7{1'b0}};
  assign out_6 = 7'b0111110;
  assign out_7 = 7'b0100010;
  assign out_8 = 7'b0111110;
  assign out_9 = {7{1'b0}};
  assign out_10 = 7'b0111110;
  assign out_11 = 7'b0000010;
  assign out_12 = 7'b0111110;
  assign out_13 = {7{1'b0}};
  assign out_14 = {7{1'b0}};
  assign out_15 = 7'b0111110;
  assign out_16 = 7'b0000010;
  assign out_17 = 7'b0000010;
  assign out_18 = {7{1'b0}};
  assign out_19 = 7'b0111110;
  assign out_20 = 7'b0100010;
  assign out_21 = 7'b0111110;
  assign out_22 = {7{1'b0}};
  assign out_23 = 7'b0111010;
  assign out_24 = 7'b0101010;
  assign out_25 = 7'b0101110;
  assign out_26 = {7{1'b0}};
  assign out_27 = 7'b0111110;
  assign out_28 = 7'b0101010;
  assign out_29 = 7'b0101010;
  assign out_30 = {7{1'b0}};
  assign out_31 = {7{1'b0}};
  assign out_32 = {7{1'b0}};
endmodule

module checkWL (
  input  selector,
  input  [6:0] in_2,
  input  [6:0] in_3,
  input  [6:0] in_4,
  input  [6:0] in_5,
  input  [6:0] in_6,
  input  [6:0] in_7,
  input  [6:0] in_8,
  input  [6:0] in_9,
  input  [6:0] in_10,
  input  [6:0] in_11,
  input  [6:0] in_12,
  input  [6:0] in_13,
  input  [6:0] in_14,
  input  [6:0] in_15,
  input  [6:0] in_16,
  input  [6:0] in_17,
  input  [6:0] in_18,
  input  [6:0] in_19,
  input  [6:0] in_20,
  input  [6:0] in_21,
  input  [6:0] in_22,
  input  [6:0] in_23,
  input  [6:0] in_24,
  input  [6:0] in_25,
  input  [6:0] in_26,
  input  [6:0] in_27,
  input  [6:0] in_28,
  input  [6:0] in_29,
  input  [6:0] in_30,
  input  [6:0] in_31,
  input  [6:0] in_32,
  input  [6:0] in_33,
  input  [6:0] in_34,
  input  [6:0] in_35,
  input  [6:0] in_36,
  input  [6:0] in_37,
  input  [6:0] in_38,
  input  [6:0] in_39,
  input  [6:0] in_40,
  input  [6:0] in_41,
  input  [6:0] in_42,
  input  [6:0] in_43,
  input  [6:0] in_44,
  input  [6:0] in_45,
  input  [6:0] in_46,
  input  [6:0] in_47,
  input  [6:0] in_48,
  input  [6:0] in_49,
  input  [6:0] in_50,
  input  [6:0] in_51,
  input  [6:0] in_52,
  input  [6:0] in_53,
  input  [6:0] in_54,
  input  [6:0] in_55,
  input  [6:0] in_56,
  input  [6:0] in_57,
  input  [6:0] in_58,
  input  [6:0] in_59,
  input  [6:0] in_60,
  input  [6:0] in_61,
  input  [6:0] in_62,
  input  [6:0] in_63,
  input  [6:0] in_64,
  input  [6:0] in_65,
  output [6:0] out_66,
  output [6:0] out_67,
  output [6:0] out_68,
  output [6:0] out_69,
  output [6:0] out_70,
  output [6:0] out_71,
  output [6:0] out_72,
  output [6:0] out_73,
  output [6:0] out_74,
  output [6:0] out_75,
  output [6:0] out_76,
  output [6:0] out_77,
  output [6:0] out_78,
  output [6:0] out_79,
  output [6:0] out_80,
  output [6:0] out_81,
  output [6:0] out_82,
  output [6:0] out_83,
  output [6:0] out_84,
  output [6:0] out_85,
  output [6:0] out_86,
  output [6:0] out_87,
  output [6:0] out_88,
  output [6:0] out_89,
  output [6:0] out_90,
  output [6:0] out_91,
  output [6:0] out_92,
  output [6:0] out_93,
  output [6:0] out_94,
  output [6:0] out_95,
  output [6:0] out_96,
  output [6:0] out_97
);

  Multiplexer #(.width(7), .enable("false")) multiplexer_1 (.in0(in_2), .in1(in_3), .out(out_66), .sel(selector));
  Multiplexer #(.width(7), .enable("false")) multiplexer_2 (.in0(in_4), .in1(in_5), .out(out_67), .sel(selector));
  Multiplexer #(.width(7), .enable("false")) multiplexer_3 (.in0(in_6), .in1(in_7), .out(out_68), .sel(selector));
  Multiplexer #(.width(7), .enable("false")) multiplexer_4 (.in0(in_8), .in1(in_9), .out(out_69), .sel(selector));
  Multiplexer #(.width(7), .enable("false")) multiplexer_5 (.in0(in_10), .in1(in_11), .out(out_70), .sel(selector));
  Multiplexer #(.width(7), .enable("false")) multiplexer_6 (.in0(in_12), .in1(in_13), .out(out_71), .sel(selector));
  Multiplexer #(.width(7), .enable("false")) multiplexer_7 (.in0(in_14), .in1(in_15), .out(out_72), .sel(selector));
  Multiplexer #(.width(7), .enable("false")) multiplexer_8 (.in0(in_16), .in1(in_17), .out(out_73), .sel(selector));
  Multiplexer #(.width(7), .enable("false")) multiplexer_9 (.in0(in_18), .in1(in_19), .out(out_74), .sel(selector));
  Multiplexer #(.width(7), .enable("false")) multiplexer_10 (.in0(in_20), .in1(in_21), .out(out_75), .sel(selector));
  Multiplexer #(.width(7), .enable("false")) multiplexer_11 (.in0(in_22), .in1(in_23), .out(out_76), .sel(selector));
  Multiplexer #(.width(7), .enable("false")) multiplexer_12 (.in0(in_24), .in1(in_25), .out(out_77), .sel(selector));
  Multiplexer #(.width(7), .enable("false")) multiplexer_13 (.in0(in_26), .in1(in_27), .out(out_78), .sel(selector));
  Multiplexer #(.width(7), .enable("false")) multiplexer_14 (.in0(in_28), .in1(in_29), .out(out_79), .sel(selector));
  Multiplexer #(.width(7), .enable("false")) multiplexer_15 (.in0(in_30), .in1(in_31), .out(out_80), .sel(selector));
  Multiplexer #(.width(7), .enable("false")) multiplexer_16 (.in0(in_32), .in1(in_33), .out(out_81), .sel(selector));
  Multiplexer #(.width(7), .enable("false")) multiplexer_17 (.in0(in_34), .in1(in_35), .out(out_82), .sel(selector));
  Multiplexer #(.width(7), .enable("false")) multiplexer_18 (.in0(in_36), .in1(in_37), .out(out_83), .sel(selector));
  Multiplexer #(.width(7), .enable("false")) multiplexer_19 (.in0(in_38), .in1(in_39), .out(out_84), .sel(selector));
  Multiplexer #(.width(7), .enable("false")) multiplexer_20 (.in0(in_40), .in1(in_41), .out(out_85), .sel(selector));
  Multiplexer #(.width(7), .enable("false")) multiplexer_21 (.in0(in_42), .in1(in_43), .out(out_86), .sel(selector));
  Multiplexer #(.width(7), .enable("false")) multiplexer_22 (.in0(in_44), .in1(in_45), .out(out_87), .sel(selector));
  Multiplexer #(.width(7), .enable("false")) multiplexer_23 (.in0(in_46), .in1(in_47), .out(out_88), .sel(selector));
  Multiplexer #(.width(7), .enable("false")) multiplexer_24 (.in0(in_48), .in1(in_49), .out(out_89), .sel(selector));
  Multiplexer #(.width(7), .enable("false")) multiplexer_25 (.in0(in_50), .in1(in_51), .out(out_90), .sel(selector));
  Multiplexer #(.width(7), .enable("false")) multiplexer_26 (.in0(in_52), .in1(in_53), .out(out_91), .sel(selector));
  Multiplexer #(.width(7), .enable("false")) multiplexer_27 (.in0(in_54), .in1(in_55), .out(out_92), .sel(selector));
  Multiplexer #(.width(7), .enable("false")) multiplexer_28 (.in0(in_56), .in1(in_57), .out(out_93), .sel(selector));
  Multiplexer #(.width(7), .enable("false")) multiplexer_29 (.in0(in_58), .in1(in_59), .out(out_94), .sel(selector));
  Multiplexer #(.width(7), .enable("false")) multiplexer_30 (.in0(in_60), .in1(in_61), .out(out_95), .sel(selector));
  Multiplexer #(.width(7), .enable("false")) multiplexer_31 (.in0(in_62), .in1(in_63), .out(out_96), .sel(selector));
  Multiplexer #(.width(7), .enable("false")) multiplexer_32 (.in0(in_64), .in1(in_65), .out(out_97), .sel(selector));
endmodule

module win_lose (
  input  selector,
  output [6:0] out_2,
  output [6:0] out_3,
  output [6:0] out_4,
  output [6:0] out_5,
  output [6:0] out_6,
  output [6:0] out_7,
  output [6:0] out_8,
  output [6:0] out_9,
  output [6:0] out_10,
  output [6:0] out_11,
  output [6:0] out_12,
  output [6:0] out_13,
  output [6:0] out_14,
  output [6:0] out_15,
  output [6:0] out_16,
  output [6:0] out_17,
  output [6:0] out_18,
  output [6:0] out_19,
  output [6:0] out_20,
  output [6:0] out_21,
  output [6:0] out_22,
  output [6:0] out_23,
  output [6:0] out_24,
  output [6:0] out_25,
  output [6:0] out_26,
  output [6:0] out_27,
  output [6:0] out_28,
  output [6:0] out_29,
  output [6:0] out_30,
  output [6:0] out_31,
  output [6:0] out_32,
  output [6:0] out_33
);

  wire [6:0] lose_1_out_1, lose_1_out_2, lose_1_out_3, lose_1_out_4, lose_1_out_5, lose_1_out_6,
       lose_1_out_7, lose_1_out_8, lose_1_out_9, lose_1_out_10, lose_1_out_11, lose_1_out_12, lose_1_out_13,
       lose_1_out_14, lose_1_out_15, lose_1_out_16, lose_1_out_17, lose_1_out_18, lose_1_out_19,
       lose_1_out_20, lose_1_out_21, lose_1_out_22, lose_1_out_23, lose_1_out_24, lose_1_out_25,
       lose_1_out_26, lose_1_out_27, lose_1_out_28, lose_1_out_29, lose_1_out_30, lose_1_out_31,
       lose_1_out_32, win_1_out_1, win_1_out_2, win_1_out_3, win_1_out_4, win_1_out_5, win_1_out_6,
       win_1_out_7, win_1_out_8, win_1_out_9, win_1_out_10, win_1_out_11, win_1_out_12, win_1_out_13,
       win_1_out_14, win_1_out_15, win_1_out_16, win_1_out_17, win_1_out_18, win_1_out_19, win_1_out_20,
       win_1_out_21, win_1_out_22, win_1_out_23, win_1_out_24, win_1_out_25, win_1_out_26, win_1_out_27,
       win_1_out_28, win_1_out_29, win_1_out_30, win_1_out_31, win_1_out_32;

  lose lose_1 (
    .out_1(lose_1_out_1), .out_2(lose_1_out_2), .out_3(lose_1_out_3), .out_4(lose_1_out_4),
    .out_5(lose_1_out_5), .out_6(lose_1_out_6), .out_7(lose_1_out_7), .out_8(lose_1_out_8),
    .out_9(lose_1_out_9), .out_10(lose_1_out_10), .out_11(lose_1_out_11), .out_12(lose_1_out_12),
    .out_13(lose_1_out_13), .out_14(lose_1_out_14), .out_15(lose_1_out_15), .out_16(lose_1_out_16),
    .out_17(lose_1_out_17), .out_18(lose_1_out_18), .out_19(lose_1_out_19), .out_20(lose_1_out_20),
    .out_21(lose_1_out_21), .out_22(lose_1_out_22), .out_23(lose_1_out_23), .out_24(lose_1_out_24),
    .out_25(lose_1_out_25), .out_26(lose_1_out_26), .out_27(lose_1_out_27), .out_28(lose_1_out_28),
    .out_29(lose_1_out_29), .out_30(lose_1_out_30), .out_31(lose_1_out_31), .out_32(lose_1_out_32));
  win win_1 (
    .out_1(win_1_out_1), .out_2(win_1_out_2), .out_3(win_1_out_3), .out_4(win_1_out_4), .out_5(win_1_out_5),
    .out_6(win_1_out_6), .out_7(win_1_out_7), .out_8(win_1_out_8), .out_9(win_1_out_9),
    .out_10(win_1_out_10), .out_11(win_1_out_11), .out_12(win_1_out_12), .out_13(win_1_out_13),
    .out_14(win_1_out_14), .out_15(win_1_out_15), .out_16(win_1_out_16), .out_17(win_1_out_17),
    .out_18(win_1_out_18), .out_19(win_1_out_19), .out_20(win_1_out_20), .out_21(win_1_out_21),
    .out_22(win_1_out_22), .out_23(win_1_out_23), .out_24(win_1_out_24), .out_25(win_1_out_25),
    .out_26(win_1_out_26), .out_27(win_1_out_27), .out_28(win_1_out_28), .out_29(win_1_out_29),
    .out_30(win_1_out_30), .out_31(win_1_out_31), .out_32(win_1_out_32));
  checkWL checkwl_1 (
    .in_2(lose_1_out_1), .in_3(win_1_out_1), .in_4(lose_1_out_2), .in_5(win_1_out_2), .in_6(lose_1_out_3),
    .in_7(win_1_out_3), .in_8(lose_1_out_4), .in_9(win_1_out_4), .in_10(lose_1_out_5), .in_11(win_1_out_5),
    .in_12(lose_1_out_6), .in_13(win_1_out_6), .in_14(lose_1_out_7), .in_15(win_1_out_7),
    .in_16(lose_1_out_8), .in_17(win_1_out_8), .in_18(lose_1_out_9), .in_19(win_1_out_9),
    .in_20(lose_1_out_10), .in_21(win_1_out_10), .in_22(lose_1_out_11), .in_23(win_1_out_11),
    .in_24(lose_1_out_12), .in_25(win_1_out_12), .in_26(lose_1_out_13), .in_27(win_1_out_13),
    .in_28(lose_1_out_14), .in_29(win_1_out_14), .in_30(lose_1_out_15), .in_31(win_1_out_15),
    .in_32(lose_1_out_16), .in_33(win_1_out_16), .in_34(lose_1_out_17), .in_35(win_1_out_17),
    .in_36(lose_1_out_18), .in_37(win_1_out_18), .in_38(lose_1_out_19), .in_39(win_1_out_19),
    .in_40(lose_1_out_20), .in_41(win_1_out_20), .in_42(lose_1_out_21), .in_43(win_1_out_21),
    .in_44(lose_1_out_22), .in_45(win_1_out_22), .in_46(lose_1_out_23), .in_47(win_1_out_23),
    .in_48(lose_1_out_24), .in_49(win_1_out_24), .in_50(lose_1_out_25), .in_51(win_1_out_25),
    .in_52(lose_1_out_26), .in_53(win_1_out_26), .in_54(lose_1_out_27), .in_55(win_1_out_27),
    .in_56(lose_1_out_28), .in_57(win_1_out_28), .in_58(lose_1_out_29), .in_59(win_1_out_29),
    .in_60(lose_1_out_30), .in_61(win_1_out_30), .in_62(lose_1_out_31), .in_63(win_1_out_31),
    .in_64(lose_1_out_32), .in_65(win_1_out_32), .out_66(out_2), .out_67(out_3), .out_68(out_4),
    .out_69(out_5), .out_70(out_6), .out_71(out_7), .out_72(out_8), .out_73(out_9), .out_74(out_10),
    .out_75(out_11), .out_76(out_12), .out_77(out_13), .out_78(out_14), .out_79(out_15), .out_80(out_16),
    .out_81(out_17), .out_82(out_18), .out_83(out_19), .out_84(out_20), .out_85(out_21), .out_86(out_22),
    .out_87(out_23), .out_88(out_24), .out_89(out_25), .out_90(out_26), .out_91(out_27), .out_92(out_28),
    .out_93(out_29), .out_94(out_30), .out_95(out_31), .out_96(out_32), .out_97(out_33), .selector(selector));
endmodule

module checkGame (
  input  in_1,
  input  in_2,
  output [6:0] out_3,
  output [6:0] out_4,
  output [6:0] out_5,
  output [6:0] out_6,
  output [6:0] out_7,
  output [6:0] out_8,
  output [6:0] out_9,
  output [6:0] out_10,
  output [6:0] out_11,
  output [6:0] out_12,
  output [6:0] out_13,
  output [6:0] out_14,
  output [6:0] out_15,
  output [6:0] out_16,
  output [6:0] out_17,
  output [6:0] out_18,
  output [6:0] out_19,
  output [6:0] out_20,
  output [6:0] out_21,
  output [6:0] out_22,
  output [6:0] out_23,
  output [6:0] out_24,
  output [6:0] out_25,
  output [6:0] out_26,
  output [6:0] out_27,
  output [6:0] out_28,
  output [6:0] out_29,
  output [6:0] out_30,
  output [6:0] out_31,
  output [6:0] out_32,
  output [6:0] out_33,
  output [6:0] out_34
);

  wire [6:0] win_lose_1_out_2, win_lose_1_out_3, win_lose_1_out_4, win_lose_1_out_5, win_lose_1_out_6,
       win_lose_1_out_7, win_lose_1_out_8, win_lose_1_out_9, win_lose_1_out_10, win_lose_1_out_11,
       win_lose_1_out_12, win_lose_1_out_13, win_lose_1_out_14, win_lose_1_out_15, win_lose_1_out_16,
       win_lose_1_out_17, win_lose_1_out_18, win_lose_1_out_19, win_lose_1_out_20, win_lose_1_out_21,
       win_lose_1_out_22, win_lose_1_out_23, win_lose_1_out_24, win_lose_1_out_25, win_lose_1_out_26,
       win_lose_1_out_27, win_lose_1_out_28, win_lose_1_out_29, win_lose_1_out_30, win_lose_1_out_31,
       win_lose_1_out_32, win_lose_1_out_33;

  win_lose win_lose_1 (
    .out_2(win_lose_1_out_2), .out_3(win_lose_1_out_3), .out_4(win_lose_1_out_4), .out_5(win_lose_1_out_5),
    .out_6(win_lose_1_out_6), .out_7(win_lose_1_out_7), .out_8(win_lose_1_out_8), .out_9(win_lose_1_out_9),
    .out_10(win_lose_1_out_10), .out_11(win_lose_1_out_11), .out_12(win_lose_1_out_12),
    .out_13(win_lose_1_out_13), .out_14(win_lose_1_out_14), .out_15(win_lose_1_out_15),
    .out_16(win_lose_1_out_16), .out_17(win_lose_1_out_17), .out_18(win_lose_1_out_18),
    .out_19(win_lose_1_out_19), .out_20(win_lose_1_out_20), .out_21(win_lose_1_out_21),
    .out_22(win_lose_1_out_22), .out_23(win_lose_1_out_23), .out_24(win_lose_1_out_24),
    .out_25(win_lose_1_out_25), .out_26(win_lose_1_out_26), .out_27(win_lose_1_out_27),
    .out_28(win_lose_1_out_28), .out_29(win_lose_1_out_29), .out_30(win_lose_1_out_30),
    .out_31(win_lose_1_out_31), .out_32(win_lose_1_out_32), .out_33(win_lose_1_out_33), .selector(in_1));
  Multiplexer #(.width(7), .enable("false")) multiplexer_1 (
    .in0({7{1'b0}}), .in1(win_lose_1_out_2), .out(out_3), .sel(in_2));
  Multiplexer #(.width(7), .enable("false")) multiplexer_2 (
    .in0({7{1'b0}}), .in1(win_lose_1_out_3), .out(out_4), .sel(in_2));
  Multiplexer #(.width(7), .enable("false")) multiplexer_3 (
    .in0({7{1'b0}}), .in1(win_lose_1_out_4), .out(out_5), .sel(in_2));
  Multiplexer #(.width(7), .enable("false")) multiplexer_4 (
    .in0({7{1'b0}}), .in1(win_lose_1_out_5), .out(out_6), .sel(in_2));
  Multiplexer #(.width(7), .enable("false")) multiplexer_5 (
    .in0({7{1'b0}}), .in1(win_lose_1_out_6), .out(out_7), .sel(in_2));
  Multiplexer #(.width(7), .enable("false")) multiplexer_6 (
    .in0({7{1'b0}}), .in1(win_lose_1_out_7), .out(out_8), .sel(in_2));
  Multiplexer #(.width(7), .enable("false")) multiplexer_7 (
    .in0({7{1'b0}}), .in1(win_lose_1_out_8), .out(out_9), .sel(in_2));
  Multiplexer #(.width(7), .enable("false")) multiplexer_8 (
    .in0({7{1'b0}}), .in1(win_lose_1_out_9), .out(out_10), .sel(in_2));
  Multiplexer #(.width(7), .enable("false")) multiplexer_9 (
    .in0({7{1'b0}}), .in1(win_lose_1_out_10), .out(out_11), .sel(in_2));
  Multiplexer #(.width(7), .enable("false")) multiplexer_10 (
    .in0({7{1'b0}}), .in1(win_lose_1_out_11), .out(out_12), .sel(in_2));
  Multiplexer #(.width(7), .enable("false")) multiplexer_11 (
    .in0({7{1'b0}}), .in1(win_lose_1_out_12), .out(out_13), .sel(in_2));
  Multiplexer #(.width(7), .enable("false")) multiplexer_12 (
    .in0({7{1'b0}}), .in1(win_lose_1_out_13), .out(out_14), .sel(in_2));
  Multiplexer #(.width(7), .enable("false")) multiplexer_13 (
    .in0({7{1'b0}}), .in1(win_lose_1_out_14), .out(out_15), .sel(in_2));
  Multiplexer #(.width(7), .enable("false")) multiplexer_14 (
    .in0({7{1'b0}}), .in1(win_lose_1_out_15), .out(out_16), .sel(in_2));
  Multiplexer #(.width(7), .enable("false")) multiplexer_15 (
    .in0({7{1'b0}}), .in1(win_lose_1_out_16), .out(out_17), .sel(in_2));
  Multiplexer #(.width(7), .enable("false")) multiplexer_16 (
    .in0({7{1'b0}}), .in1(win_lose_1_out_17), .out(out_18), .sel(in_2));
  Multiplexer #(.width(7), .enable("false")) multiplexer_17 (
    .in0({7{1'b0}}), .in1(win_lose_1_out_18), .out(out_19), .sel(in_2));
  Multiplexer #(.width(7), .enable("false")) multiplexer_18 (
    .in0({7{1'b0}}), .in1(win_lose_1_out_19), .out(out_20), .sel(in_2));
  Multiplexer #(.width(7), .enable("false")) multiplexer_19 (
    .in0({7{1'b0}}), .in1(win_lose_1_out_20), .out(out_21), .sel(in_2));
  Multiplexer #(.width(7), .enable("false")) multiplexer_20 (
    .in0({7{1'b0}}), .in1(win_lose_1_out_21), .out(out_22), .sel(in_2));
  Multiplexer #(.width(7), .enable("false")) multiplexer_21 (
    .in0({7{1'b0}}), .in1(win_lose_1_out_22), .out(out_23), .sel(in_2));
  Multiplexer #(.width(7), .enable("false")) multiplexer_22 (
    .in0({7{1'b0}}), .in1(win_lose_1_out_23), .out(out_24), .sel(in_2));
  Multiplexer #(.width(7), .enable("false")) multiplexer_23 (
    .in0({7{1'b0}}), .in1(win_lose_1_out_24), .out(out_25), .sel(in_2));
  Multiplexer #(.width(7), .enable("false")) multiplexer_24 (
    .in0({7{1'b0}}), .in1(win_lose_1_out_25), .out(out_26), .sel(in_2));
  Multiplexer #(.width(7), .enable("false")) multiplexer_25 (
    .in0({7{1'b0}}), .in1(win_lose_1_out_26), .out(out_27), .sel(in_2));
  Multiplexer #(.width(7), .enable("false")) multiplexer_26 (
    .in0({7{1'b0}}), .in1(win_lose_1_out_27), .out(out_28), .sel(in_2));
  Multiplexer #(.width(7), .enable("false")) multiplexer_27 (
    .in0({7{1'b0}}), .in1(win_lose_1_out_28), .out(out_29), .sel(in_2));
  Multiplexer #(.width(7), .enable("false")) multiplexer_28 (
    .in0({7{1'b0}}), .in1(win_lose_1_out_29), .out(out_30), .sel(in_2));
  Multiplexer #(.width(7), .enable("false")) multiplexer_29 (
    .in0({7{1'b0}}), .in1(win_lose_1_out_30), .out(out_31), .sel(in_2));
  Multiplexer #(.width(7), .enable("false")) multiplexer_30 (
    .in0({7{1'b0}}), .in1(win_lose_1_out_31), .out(out_32), .sel(in_2));
  Multiplexer #(.width(7), .enable("false")) multiplexer_31 (
    .in0({7{1'b0}}), .in1(win_lose_1_out_32), .out(out_33), .sel(in_2));
  Multiplexer #(.width(7), .enable("false")) multiplexer_32 (
    .in0({7{1'b0}}), .in1(win_lose_1_out_33), .out(out_34), .sel(in_2));
endmodule

module speedUp (
  input  [3:0] clockChoose,
  output clockOut
);

  wire clock_1_out, counter_1_carry, counter_2_carry, counter_3_carry;

  Clock clock_1 (.out(clock_1_out));
  Counter #(.max('h1)) counter_1 (.carry(counter_1_carry), .clk(clock_1_out));  // open: load, D, count, Q, clr
  Counter #(.max('h1)) counter_2 (.carry(counter_2_carry), .clk(counter_1_carry));  // open: load, D, count, Q, clr
  Counter #(.max('h1)) counter_3 (.carry(counter_3_carry), .clk(counter_2_carry));  // open: load, D, count, Q, clr
  Counter #(.max('h1)) counter_4 (.clk(counter_3_carry));  // open: load, D, count, Q, carry, clr
  Multiplexer #(.select(4), .enable("false")) multiplexer_1 (
    .in0(counter_3_carry), .in1(counter_3_carry), .in2(counter_2_carry), .in3(counter_1_carry),
    .in4(clock_1_out), .out(clockOut), .sel(clockChoose));  // open: in5, in6, in7, in8, in9, in10, in11, in12, in13, in14, in15
endmodule

module disablers (
  input  upIn,
  input  downIn,
  input  rightIn,
  input  leftIn,
  input  enable,
  output upOut,
  output downOut,
  output rightOut,
  output leftOut
);

  Multiplexer #(.enable("false")) multiplexer_1 (.in0(upIn), .out(upOut), .sel(enable));  // open: in1
  Multiplexer #(.enable("false")) multiplexer_2 (.in0(downIn), .out(downOut), .sel(enable));  // open: in1
  Multiplexer #(.enable("false")) multiplexer_3 (.in0(rightIn), .out(rightOut), .sel(enable));  // open: in1
  Multiplexer #(.enable("false")) multiplexer_4 (.in0(leftIn), .out(leftOut), .sel(enable));  // open: in1
endmodule
